// Logisim project Proiect_incuietoare.circ as structural Verilog
module main (
  output [6:0] catod,
  output [7:0] anod
);

  wire AD_CIF_out, clock_1_out, comparator_4b_1_egal, comparator_4b_2_egal, comparator_4b_3_egal, DOWN_out,
       MASTER_RESET_out, RESET_out, START_out, uc_1_en_down, uc_1_en_up, uc_1_intr_cif, uc_1_liber_ocupat,
       uc_1_mem_cif1, uc_1_mem_cif2, uc_1_mem_cif3, uc_1_mem_cif4, uc_1_mem_cif5, uc_1_mem_cif6,
       uc_1_r_part_reg, uc_1_r_tot_reg, uc_1_rc, UP_out;
  wire [2:0] num_ssd_1_num;
  wire [3:0] catod_anod_1_catod, numarator_rev_1_15_1_q, registru_mem_cif_1_q, registru_mem_cif_2_q,
       registru_mem_cif_3_q, registru_mem_cif_4_q, registru_mem_cif_5_q, registru_mem_cif_6_q;

  Clock clock_1 (.out(clock_1_out));
  Button RESET (.out(RESET_out));
  Button MASTER_RESET (.out(MASTER_RESET_out));
  Button START (.out(START_out));
  Button AD_CIF (.out(AD_CIF_out));
  Button UP (.out(UP_out));
  Button DOWN (.out(DOWN_out));
  UC uc_1 (
    .start(START_out), .ad_cif(AD_CIF_out), .up(UP_out), .down(DOWN_out), .clk(clock_1_out),
    .egal1(comparator_4b_1_egal), .egal2(comparator_4b_2_egal), .egal3(comparator_4b_3_egal),
    .reset(RESET_out), .master_reset(MASTER_RESET_out), .intr_cif(uc_1_intr_cif),
    .liber_ocupat(uc_1_liber_ocupat), .en_up(uc_1_en_up), .en_down(uc_1_en_down), .mem_cif1(uc_1_mem_cif1),
    .mem_cif2(uc_1_mem_cif2), .mem_cif3(uc_1_mem_cif3), .mem_cif4(uc_1_mem_cif4), .mem_cif5(uc_1_mem_cif5),
    .mem_cif6(uc_1_mem_cif6), .RC(uc_1_rc), .r_tot_reg(uc_1_r_tot_reg), .r_part_reg(uc_1_r_part_reg));
  LED LED_1 (.in(uc_1_intr_cif));
  LED LED_2 (.in(uc_1_liber_ocupat));
  Numarator_rev_1_15 numarator_rev_1_15_1 (
    .en_up(uc_1_en_up), .en_down(uc_1_en_down), .load(uc_1_rc), .clk(clock_1_out), .q(numarator_rev_1_15_1_q));
  num_ssd num_ssd_1 (.clk(clock_1_out), .num(num_ssd_1_num));
  Registru_mem_cif registru_mem_cif_1 (
    .d(numarator_rev_1_15_1_q), .mem_cif(uc_1_mem_cif1), .clk(clock_1_out), .reset(uc_1_r_tot_reg),
    .q(registru_mem_cif_1_q));
  Registru_mem_cif registru_mem_cif_2 (
    .d(numarator_rev_1_15_1_q), .mem_cif(uc_1_mem_cif4), .clk(clock_1_out), .reset(uc_1_r_part_reg),
    .q(registru_mem_cif_2_q));
  Registru_mem_cif registru_mem_cif_3 (
    .d(numarator_rev_1_15_1_q), .mem_cif(uc_1_mem_cif2), .clk(clock_1_out), .reset(uc_1_r_tot_reg),
    .q(registru_mem_cif_3_q));
  Registru_mem_cif registru_mem_cif_4 (
    .d(numarator_rev_1_15_1_q), .mem_cif(uc_1_mem_cif5), .clk(clock_1_out), .reset(uc_1_r_part_reg),
    .q(registru_mem_cif_4_q));
  Registru_mem_cif registru_mem_cif_5 (
    .d(numarator_rev_1_15_1_q), .mem_cif(uc_1_mem_cif3), .clk(clock_1_out), .reset(uc_1_r_tot_reg),
    .q(registru_mem_cif_5_q));
  Registru_mem_cif registru_mem_cif_6 (
    .d(numarator_rev_1_15_1_q), .mem_cif(uc_1_mem_cif6), .clk(clock_1_out), .reset(uc_1_r_part_reg),
    .q(registru_mem_cif_6_q));
  catod_anod catod_anod_1 (
    .s(num_ssd_1_num), .clk(clock_1_out), .liber_ocupat(uc_1_liber_ocupat), .d0(registru_mem_cif_1_q),
    .d1(registru_mem_cif_3_q), .d2(registru_mem_cif_5_q), .d3(registru_mem_cif_2_q),
    .d4(registru_mem_cif_4_q), .d5(registru_mem_cif_6_q), .q(numarator_rev_1_15_1_q), .on_off(uc_1_intr_cif),
    .catod(catod_anod_1_catod), .anod(anod));
  Comparator_4b comparator_4b_1 (.a(registru_mem_cif_1_q), .b(registru_mem_cif_2_q), .egal(comparator_4b_1_egal));
  Comparator_4b comparator_4b_2 (.a(registru_mem_cif_3_q), .b(registru_mem_cif_4_q), .egal(comparator_4b_2_egal));
  Comparator_4b comparator_4b_3 (.a(registru_mem_cif_5_q), .b(registru_mem_cif_6_q), .egal(comparator_4b_3_egal));
  SSD_DEC ssd_dec_1 (.nr(catod_anod_1_catod), .q(catod));
endmodule

// VHDL entity Numarator_rev_1_15, as the project stores it:
LIBRARY ieee;
USE ieee.std_logic_1164.all;
USE ieee.std_logic_unsigned.all;

ENTITY Numarator_rev_1_15 IS
	PORT(en_up : in std_logic;
  		en_down : in std_logic;
  		load : in std_logic;
  		clk : in std_logic;
  		q : out std_logic_vector(3 downto 0));
END Numarator_rev_1_15;


ARCHITECTURE TypeArchitecture OF Numarator_rev_1_15 IS

signal aux : std_logic_vector(3 downto 0) := "0001";

BEGIN
	process(clk)
	begin
			if load = '1' then aux <= "0001";
			elsif en_up = '1' then
				if aux = "1111" then aux <= "0001";
				else aux <= aux + 1;
				end if;
			elsif en_down = '1' then 
				if aux = "0001" then aux <= "1111";
				else aux <= aux - 1;
				end if;
			end if;
		q <= aux;
	end process;

END TypeArchitecture;

// VHDL entity Registru_mem_cif, as the project stores it:
LIBRARY ieee;
USE ieee.std_logic_1164.all;
USE ieee.std_logic_unsigned.all;

ENTITY Registru_mem_cif IS
	PORT(d : in std_logic_vector(3 downto 0);
		mem_cif : in std_logic;
		clk : in std_logic;
		q : out std_logic_vector(3 downto 0);
		reset : in std_logic);
END Registru_mem_cif;

ARCHITECTURE TypeArchitecture OF Registru_mem_cif IS

signal aux : std_logic_vector(3 downto 0) := (others => '0');

BEGIN
	
	process(clk)
	begin
		if clk'event and clk = '1' and mem_cif = '1' then
			aux <= d;
		end if;

		if aux = "UUUU" or reset = '1' then aux <= x"0";
		end if;

		q <= aux;
	end process;

END TypeArchitecture;

// VHDL entity Comparator_4b, as the project stores it:
LIBRARY ieee;
USE ieee.std_logic_1164.all;

ENTITY Comparator_4b IS
	PORT(a : in std_logic_vector(3 downto 0);
		b : in std_logic_vector(3 downto 0);
		egal : out std_logic);
END Comparator_4b;

ARCHITECTURE TypeArchitecture OF Comparator_4b IS

BEGIN

	process(a, b)
	begin
		if a = b then egal <= '1';
		else egal <= '0';
		end if;
	end process;

END TypeArchitecture;

// VHDL entity UC, as the project stores it:
LIBRARY ieee;
USE ieee.std_logic_1164.all;

ENTITY UC IS
	PORT(start : in std_logic;
		ad_cif : in std_logic;
		up : in std_logic;
		down : in std_logic;
		clk : in std_logic;
		intr_cif : out std_logic;
		liber_ocupat : inout std_logic;
		egal1, egal2, egal3 : in std_logic;
		reset : in std_logic;
		master_reset : in std_logic;
		en_up : out std_logic;
		en_down : out std_logic;
		mem_cif1 : out std_logic;
		mem_cif2 : out std_logic;
		mem_cif3 : out std_logic;
		mem_cif4 : out std_logic;
		mem_cif5 : out std_logic;
		mem_cif6 : out std_logic;
		RC : out std_logic;
		r_tot_reg : out std_logic;
		r_part_reg : out std_logic);
END UC;

ARCHITECTURE TypeArchitecture OF UC IS

type mod_stare is (ST0, ST1, ST2, ST3, ST4, ST5, ST6, ST7, ST8, ST9, ST10, ST11, ST12, ST13, ST14, ST15);

signal stare, nxstare : mod_stare;

signal verod_cif : std_logic := '0';

BEGIN

	act_stare: process(clk)
	begin
		if clk'event and clk = '1' then
			stare <= nxstare;
		end if;
	end process;

	trans_stare: process(stare, clk)
	begin

	en_up <= '0';
	en_down <= '0';

	if clk = '1' then
		intr_cif <= '0';
		liber_ocupat <= '0';
		mem_cif1 <= '0';
		mem_cif2 <= '0';
		mem_cif3 <= '0';
		mem_cif4 <= '0';
		mem_cif5 <= '0';
		mem_cif6 <= '0';
		RC <= '0';
		r_tot_reg <= '0';
		r_part_reg <= '0';

		case stare is
			when ST0 =>
				if start = '1' then
					nxstare <= ST1;
				end if;
			when ST1 =>
				if ad_cif = '1' then
					intr_cif <= '1';	nxstare <= ST2;
				end if;
			when ST2 =>							--cif1
				intr_cif <= '1';
				if ad_cif = '0' then verod_cif <= '1';
				end if;

				if ad_cif = '1' and verod_cif = '1' then
					mem_cif1 <= '1';	RC <= '1';	verod_cif <= '0';	nxstare <= ST4;
				end if;
				if up = '1' then
					en_up <= '1';
					nxstare <= ST3;
				elsif down = '1' then
					en_down <= '1';
					nxstare <= ST3;
				end if;
			when ST3 =>
				intr_cif <= '1';
				if up = '0' and down = '0' then
				
					if ad_cif = '1' then
						mem_cif1 <= '1';	RC <= '1';
						nxstare <= ST4;
					else
						nxstare <= ST2;
					end if;
				end if;
			when ST4 =>						--cif2
				intr_cif <= '1';
				if ad_cif = '0' then verod_cif <= '1';
				end if;

				if ad_cif = '1' and verod_cif = '1' then
					mem_cif2 <= '1';	RC <= '1';	verod_cif <= '0';	nxstare <= ST6;
				end if;				
				if up = '1' then
					en_up <= '1';
					nxstare <= ST5;
				elsif down = '1' then
					en_down <= '1';
					nxstare <= ST5;
				end if;
			when ST5 =>
				intr_cif <= '1';
				if up = '0' and down = '0' then
					if ad_cif = '1' then
						mem_cif2 <= '1';	RC <= '1';
						nxstare <= ST6;
					else
						nxstare <= ST4;
					end if;
				end if;
			when ST6 =>						--cif3
				intr_cif <= '1';
				if ad_cif = '0' then verod_cif <= '1';
				end if;

				if ad_cif = '1' and verod_cif = '1' then
					mem_cif3 <= '1';	RC <= '1';	verod_cif <= '0';	nxstare <= ST8;
				end if;
				if up = '1' then
					en_up <= '1';
					nxstare <= ST7;
				elsif down = '1' then
					en_down <= '1';
					nxstare <= ST7;
				end if;
			when ST7 =>
				intr_cif <= '1';
				if up = '0' and down = '0' then
					if ad_cif = '1' then
						mem_cif3 <= '1';	RC <= '1';
						nxstare <= ST8;
					else
						nxstare <= ST6;
					end if;
				end if;
			when ST8 =>							--blocat
				liber_ocupat <= '1';
				if ad_cif = '1' then
					nxstare <= ST9;
				end if;
			when ST9 =>							--cif1vf
				liber_ocupat <= '1';
				intr_cif <= '1';
				if ad_cif = '0' then verod_cif <= '1';
				end if;

				if ad_cif = '1' and verod_cif = '1' then
					mem_cif4 <= '1';	RC <= '1';	verod_cif <= '0';	nxstare <= ST11;
				end if;
				
				if up = '1' then
					en_up <= '1';
					nxstare <= ST10;
				elsif down = '1' then
					en_down <= '1';
					nxstare <= ST10;
				end if;
			when ST10 =>
				liber_ocupat <= '1';
				intr_cif <= '1';
				
				if up = '0' and down = '0' then
					if ad_cif = '1' then
						mem_cif4 <= '1';	RC <= '1';
						nxstare <= ST11;
					else
						nxstare <= ST9;
					end if;
				end if;
			when ST11 =>							--cif2vf
				liber_ocupat <= '1';
				intr_cif <= '1';
				if ad_cif = '0' then verod_cif <= '1';
				end if;

				if ad_cif = '1' and verod_cif = '1' then
					mem_cif5 <= '1';	RC <= '1';	verod_cif <= '0';	nxstare <= ST13;
				end if;
				
				if up = '1' then
					en_up <= '1';
					nxstare <= ST12;
				elsif down = '1' then
					en_down <= '1';
					nxstare <= ST12;
				end if;
			when ST12 =>
				liber_ocupat <= '1';
				intr_cif <= '1';
				
				if up = '0' and down = '0' then
					if ad_cif = '1' then
						mem_cif5 <= '1';	RC <= '1';
						nxstare <= ST13;
					else
						nxstare <= ST11;
					end if;
				end if;
			when ST13 =>							--cif3vf
				liber_ocupat <= '1';
				intr_cif <= '1';
				if ad_cif = '0' then verod_cif <= '1';
				end if;

				if ad_cif = '1' and verod_cif = '1' then
					mem_cif6 <= '1';	RC <= '1';	verod_cif <= '0';	nxstare <= ST15;
				end if;
				
				if up = '1' then
					en_up <= '1';
					nxstare <= ST14;
				elsif down = '1' then
					en_down <= '1';
					nxstare <= ST14;
				end if;
			when ST14 =>
				liber_ocupat <= '1';
				intr_cif <= '1';
				
				if up = '0' and down = '0' then
					if ad_cif = '1' then
						mem_cif6 <= '1';	RC <= '1';
						nxstare <= ST15;
					else
						nxstare <= ST13;
					end if;
				end if;
			when ST15 =>								--vf deblocare/ revenire in starea initiala
				liber_ocupat <= '1';
				if egal1 = '1' and egal2 = '1' and egal3 = '1' then
					nxstare <= ST1;	r_tot_reg <= '1';	r_part_reg <= '1';
				else
					nxstare <= ST8;	r_part_reg <= '1';
				end if;
		end case;

		if reset = '1'	then
			RC <= '1';
			if liber_ocupat = '0' then nxstare <= ST2;	r_tot_reg <= '1';
			else nxstare <= ST9;	r_part_reg <= '1';
			end if;
		end if;

		if master_reset = '1' then nxstare <= ST2;	RC <= '1';	r_tot_reg <= '1';	r_part_reg <= '1';
		end if;

	end if;
	end process;

END TypeArchitecture;

// VHDL entity SSD_DEC, as the project stores it:
LIBRARY ieee;
USE ieee.std_logic_1164.all;

ENTITY SSD_DEC IS
	PORT(nr : in std_logic_vector(3 downto 0);
		q : inout std_logic_vector(6 downto 0));			
END SSD_DEC;

ARCHITECTURE TypeArchitecture OF SSD_DEC IS

BEGIN

	process(nr)

	variable aux : std_logic_vector(6 downto 0) := (others => '0');
	
	begin
		case nr is
			when x"0" =>  aux := "0000000";
   	 		when x"1" =>  aux := "0110000";
    			when x"2" =>  aux := "1101101";
    			when x"3" =>  aux := "1111001";
    			when x"4" =>  aux := "0110011";
    			when x"5" =>  aux := "1011011";
    			when x"6" =>  aux := "1011111";
    			when x"7" =>  aux := "1110000";
    			when x"8" =>  aux := "1111111";
    			when x"9" =>  aux := "1111011";
    			when x"A" =>  aux := "1110111";
    			when x"B" =>  aux := "0011111";
    			when x"C" =>  aux := "1001110";
    			when x"D" =>  aux := "0111101";
    			when x"E" =>  aux := "1001111";
    			when others => aux := "1000111";
		end case;
		q <= aux;
	end process;
	
END TypeArchitecture;

// VHDL entity num_ssd, as the project stores it:
LIBRARY ieee;
USE ieee.std_logic_1164.all;
USE ieee.std_logic_unsigned.all;


ENTITY num_ssd IS
	PORT(clk : in std_logic;
		num : out std_logic_vector(2 downto 0));
END num_ssd;

ARCHITECTURE TypeArchitecture OF num_ssd IS

signal aux : std_logic_vector(15 downto 0) := (others => '0');

BEGIN

	process(clk)
	begin
		if clk = '1' then
			num(2) <= aux(15);
			num(1) <= aux(14);
			num(0) <= aux(13);
			aux <= aux + 1;
		end if;
	end process;

END TypeArchitecture;

// VHDL entity catod_anod, as the project stores it:
LIBRARY ieee;
USE ieee.std_logic_1164.all;
USE ieee.std_logic_unsigned.all;

ENTITY catod_anod IS
	PORT(s : in std_logic_vector(2 downto 0);
		clk : in std_logic;
		liber_ocupat : in std_logic;
		d0, d1, d2, d3, d4, d5, q : in std_logic_vector(3 downto 0);
		catod : out std_logic_vector(3 downto 0);
		anod : out std_logic_vector(7 downto 0);
		on_off : in std_logic);
END catod_anod;

ARCHITECTURE TypeArchitecture OF catod_anod IS

signal ct1, ct2 : std_logic_vector(1 downto 0) := (others => '0');

BEGIN

	process(clk)
	begin
		case s is
			when "000" =>	
				if liber_ocupat = '0' then
					if d0 /= x"0" then catod <= d0;
					else catod <= q;	end if;
				end if;
				if liber_ocupat = '1' then
					if d3 /= x"0" then catod <= d3;
					else catod <= q;	end if;
				end if;
				anod <= "11111110";
			when "001" =>		
				if liber_ocupat = '0' then
					if d1 /= x"0" or d0 = x"0" then catod <= d1;
					else catod <= q;	end if;
				end if;
				if liber_ocupat = '1' then
					if d4 /= x"0" or d3 = x"0" then catod <= d4;
					else catod <= q;	end if;
				end if;
				anod <= "11111101";
			when "010" =>	
				if liber_ocupat = '0' then
					if d2 /= x"0" or d1 = x"0" then catod <= d2;
					else catod <= q;	end if;
				end if;
				if liber_ocupat = '1' then
					if d5 /= x"0" or d4 = x"0" then catod <= d5;
					else catod <= q;	end if;
				end if;
				anod <= "11111011";
			when "011" => 
				catod <= x"0";	anod <= "11110111";
			when "100" => 
				catod <= x"0";	anod <= "11101111";
			when "101" => 
				catod <= x"0";	anod <= "11011111";
			when "110" => 
				catod <= x"0";	anod <= "10111111";
			when "111" =>
				catod <= x"0";	anod <= "01111111";
			when others =>
		end case;

		if on_off = '0' then catod <= x"0";
		end if;
	end process;

END TypeArchitecture;

// VHDL entity ssdec, as the project stores it:
LIBRARY ieee;
USE ieee.std_logic_1164.all;
USE ieee.std_logic_unsigned.all;

ENTITY ssdec IS
	PORT(nr : in std_logic_vector(6 downto 0);
		anod : in std_logic_vector(7 downto 0);
		a, b, c, d, e, f, g : out std_logic);
END ssdec;

ARCHITECTURE TypeArchitecture OF ssdec IS

BEGIN

	a <= nr(6) when anod = "11111110" else '0';
	b <= nr(5) when anod = "11111110" else '0';
	c <= nr(4) when anod = "11111110" else '0'; 
	d <= nr(3) when anod = "11111110" else '0';
	e <= nr(2) when anod = "11111110" else '0';
	f <= nr(1) when anod = "11111110" else '0';
	g <= nr(0) when anod = "11111110" else '0';

END TypeArchitecture;

// VHDL entity ssdec1, as the project stores it:
LIBRARY ieee;
USE ieee.std_logic_1164.all;
USE ieee.std_logic_unsigned.all;

ENTITY ssdec1 IS
	PORT(nr : in std_logic_vector(6 downto 0);
		anod : in std_logic_vector(7 downto 0);
		a, b, c, d, e, f, g : out std_logic);
END ssdec1;

ARCHITECTURE TypeArchitecture OF ssdec1 IS


BEGIN

	a <= nr(6) when anod = "11111101" else '0';
	b <= nr(5) when anod = "11111101" else '0';
	c <= nr(4) when anod = "11111101" else '0'; 
	d <= nr(3) when anod = "11111101" else '0';
	e <= nr(2) when anod = "11111101" else '0';
	f <= nr(1) when anod = "11111101" else '0';
	g <= nr(0) when anod = "11111101" else '0';

END TypeArchitecture;

// VHDL entity ssdec2, as the project stores it:
LIBRARY ieee;
USE ieee.std_logic_1164.all;
USE ieee.std_logic_unsigned.all;

ENTITY ssdec2 IS
	PORT(nr : in std_logic_vector(6 downto 0);
		anod : in std_logic_vector(7 downto 0);
		a, b, c, d, e, f, g : out std_logic);
END ssdec2;

ARCHITECTURE TypeArchitecture OF ssdec2 IS


BEGIN

	a <= nr(6) when anod = "11111011" else '0';
	b <= nr(5) when anod = "11111011" else '0';
	c <= nr(4) when anod = "11111011" else '0'; 
	d <= nr(3) when anod = "11111011" else '0';
	e <= nr(2) when anod = "11111011" else '0';
	f <= nr(1) when anod = "11111011" else '0';
	g <= nr(0) when anod = "11111011" else '0';

END TypeArchitecture;

// VHDL entity ssdec3, as the project stores it:
LIBRARY ieee;
USE ieee.std_logic_1164.all;
USE ieee.std_logic_unsigned.all;

ENTITY ssdec3 IS
	PORT(nr : in std_logic_vector(6 downto 0);
		anod : in std_logic_vector(7 downto 0);
		a, b, c, d, e, f, g : out std_logic);
END ssdec3;

ARCHITECTURE TypeArchitecture OF ssdec3 IS


BEGIN

	a <= nr(6) when anod = "11110111" else '0';
	b <= nr(5) when anod = "11110111" else '0';
	c <= nr(4) when anod = "11110111" else '0'; 
	d <= nr(3) when anod = "11110111" else '0';
	e <= nr(2) when anod = "11110111" else '0';
	f <= nr(1) when anod = "11110111" else '0';
	g <= nr(0) when anod = "11110111" else '0';

END TypeArchitecture;

// VHDL entity ssdec4, as the project stores it:
LIBRARY ieee;
USE ieee.std_logic_1164.all;
USE ieee.std_logic_unsigned.all;

ENTITY ssdec4 IS
	PORT(nr : in std_logic_vector(6 downto 0);
		anod : in std_logic_vector(7 downto 0);
		a, b, c, d, e, f, g : out std_logic);
END ssdec4;

ARCHITECTURE TypeArchitecture OF ssdec4 IS


BEGIN

	a <= nr(6) when anod = "11101111" else '0';
	b <= nr(5) when anod = "11101111" else '0';
	c <= nr(4) when anod = "11101111" else '0'; 
	d <= nr(3) when anod = "11101111" else '0';
	e <= nr(2) when anod = "11101111" else '0';
	f <= nr(1) when anod = "11101111" else '0';
	g <= nr(0) when anod = "11101111" else '0';

END TypeArchitecture;

// VHDL entity ssdec5, as the project stores it:
LIBRARY ieee;
USE ieee.std_logic_1164.all;
USE ieee.std_logic_unsigned.all;

ENTITY ssdec5 IS
	PORT(nr : in std_logic_vector(6 downto 0);
		anod : in std_logic_vector(7 downto 0);
		a, b, c, d, e, f, g : out std_logic);
END ssdec5;

ARCHITECTURE TypeArchitecture OF ssdec5 IS


BEGIN

	a <= nr(6) when anod = "11011111" else '0';
	b <= nr(5) when anod = "11011111" else '0';
	c <= nr(4) when anod = "11011111" else '0'; 
	d <= nr(3) when anod = "11011111" else '0';
	e <= nr(2) when anod = "11011111" else '0';
	f <= nr(1) when anod = "11011111" else '0';
	g <= nr(0) when anod = "11011111" else '0';

END TypeArchitecture;

// VHDL entity ssdec6, as the project stores it:
LIBRARY ieee;
USE ieee.std_logic_1164.all;
USE ieee.std_logic_unsigned.all;

ENTITY ssdec6 IS
	PORT(nr : in std_logic_vector(6 downto 0);
		anod : in std_logic_vector(7 downto 0);
		a, b, c, d, e, f, g : out std_logic);
END ssdec6;

ARCHITECTURE TypeArchitecture OF ssdec6 IS


BEGIN

	a <= nr(6) when anod = "10111111" else '0';
	b <= nr(5) when anod = "10111111" else '0';
	c <= nr(4) when anod = "10111111" else '0'; 
	d <= nr(3) when anod = "10111111" else '0';
	e <= nr(2) when anod = "10111111" else '0';
	f <= nr(1) when anod = "10111111" else '0';
	g <= nr(0) when anod = "10111111" else '0';

END TypeArchitecture;

// VHDL entity ssdec7, as the project stores it:
LIBRARY ieee;
USE ieee.std_logic_1164.all;
USE ieee.std_logic_unsigned.all;

ENTITY ssdec7 IS
	PORT(nr : in std_logic_vector(6 downto 0);
		anod : in std_logic_vector(7 downto 0);
		a, b, c, d, e, f, g : out std_logic);
END ssdec7;

ARCHITECTURE TypeArchitecture OF ssdec7 IS


BEGIN

	a <= nr(6) when anod = "01111111" else '0';
	b <= nr(5) when anod = "01111111" else '0';
	c <= nr(4) when anod = "01111111" else '0'; 
	d <= nr(3) when anod = "01111111" else '0';
	e <= nr(2) when anod = "01111111" else '0';
	f <= nr(1) when anod = "01111111" else '0';
	g <= nr(0) when anod = "01111111" else '0';

END TypeArchitecture;
